// Logisim project MIPS_11.circ as structural Verilog: 7 circuits, main circuit main
module main (
  input  [5:0] op,
  input  [4:0] rs,
  input  [4:0] rt,
  input  [4:0] rd,
  input  [4:0] sh,
  input  [5:0] funct
);

  wire alucontrol_1_issub, ALUsrc, cache_1_hit, clock_1_out, control_1_mem2reg, control_1_memread,
       control_1_memwrite, control_1_regwrite, RegDst;
  wire [2:0] alucontrol_1_alucode, ALUop;
  wire [4:0] multiplexer_1_out;
  wire [31:0] alu_32_1_outputt, bit_extender_1_out, cache_1_read, cache_in, cache_out, memory_1_read,
       multiplexer_2_out, multiplexer_3_out, multiplexer_4_out, registerfile_1_read1, registerfile_1_read2,
       undriven;

  Clock clock_1 (.out(clock_1_out));
  Control control_1 (
    .OPcode(op), .RegDst(RegDst), .MemWrite(control_1_memwrite), .MemRead(control_1_memread),
    .Mem2Reg(control_1_mem2reg), .RegWrite(control_1_regwrite), .ALUsrc(ALUsrc), .ALUop(ALUop));
  Multiplexer #(.width(5)) multiplexer_1 (.in0(rt), .in1(rd), .out(multiplexer_1_out), .sel(RegDst));
  assign bit_extender_1_out = {{16{1'b0}}, {rd, sh, funct}};  // Bit_Extender bit_extender_1
  RegisterFile registerfile_1 (
    .readReg2(rt), .readReg1(rs), .clk(clock_1_out), .writeReg(multiplexer_1_out),
    .writeData(multiplexer_3_out), .RegWrite(control_1_regwrite), .read1(registerfile_1_read1),
    .read2(registerfile_1_read2));
  Multiplexer #(.width(32)) multiplexer_2 (
    .in0(registerfile_1_read2), .in1(bit_extender_1_out), .out(multiplexer_2_out), .sel(ALUsrc));
  ALUcontrol alucontrol_1 (.ALUop(ALUop), .funct(funct), .isSub(alucontrol_1_issub), .ALUcode(alucontrol_1_alucode));
  ALU_32 alu_32_1 (
    .A(registerfile_1_read1), .B(multiplexer_2_out), .Sub(alucontrol_1_issub), .Op(alucontrol_1_alucode),
    .outputt(alu_32_1_outputt));
  Memory memory_1 (
    .address(alu_32_1_outputt), .data(registerfile_1_read2), .writeSignal(control_1_memwrite),
    .readSignal(control_1_memread), .clk(clock_1_out), .read(memory_1_read));
  Multiplexer #(.width(32)) multiplexer_3 (
    .in0(alu_32_1_outputt), .in1(memory_1_read), .out(multiplexer_3_out), .sel(control_1_mem2reg));
  Cache cache_1 (.clk(clock_1_out), .update(cache_out), .address(cache_in), .hit(cache_1_hit), .read(cache_1_read));
  Multiplexer #(.width(32)) multiplexer_4 (
    .in0(cache_in), .in1(cache_1_read), .out(multiplexer_4_out), .sel(cache_1_hit));
  Multiplexer #(.width(32)) multiplexer_5 (.in0(undriven), .in1(multiplexer_4_out), .out(cache_out), .sel(cache_1_hit));

  // Notes on the sheet:
  //   Cache implementation (not working)
  //   MEMORY
endmodule

module RegisterFile (
  input  [31:0] writeData,
  input  RegWrite,
  input  [4:0] readReg1,
  input  [4:0] writeReg,
  input  clk,
  input  [4:0] readReg2,
  output [31:0] read1,
  output [31:0] read2
);

  wire and_1_out, and_2_out, and_3_out, and_4_out, and_5_out, and_6_out, and_7_out, and_8_out, and_9_out,
       and_10_out, and_11_out, and_12_out, and_13_out, and_14_out, and_15_out, and_16_out, and_17_out,
       and_18_out, and_19_out, and_20_out, and_21_out, and_22_out, and_23_out, and_24_out, and_25_out,
       and_26_out, and_27_out, and_28_out, and_29_out, and_30_out, and_31_out, decoder_1_out1,
       decoder_1_out2, decoder_1_out3, decoder_1_out4, decoder_1_out5, decoder_1_out6, decoder_1_out7,
       decoder_1_out8, decoder_1_out9, decoder_1_out10, decoder_1_out11, decoder_1_out12, decoder_1_out13,
       decoder_1_out14, decoder_1_out15, decoder_1_out16, decoder_1_out17, decoder_1_out18, decoder_1_out19,
       decoder_1_out20, decoder_1_out21, decoder_1_out22, decoder_1_out23, decoder_1_out24, decoder_1_out25,
       decoder_1_out26, decoder_1_out27, decoder_1_out28, decoder_1_out29, decoder_1_out30, decoder_1_out31,
       undriven, undriven_2, undriven_3;
  wire [31:0] register_1_q, register_2_q, register_3_q, register_4_q, register_5_q, register_6_q,
       register_7_q, register_8_q, register_9_q, register_10_q, register_11_q, register_12_q, register_13_q,
       register_14_q, register_15_q, register_16_q, register_17_q, register_18_q, register_19_q,
       register_20_q, register_21_q, register_22_q, register_23_q, register_24_q, register_25_q,
       register_26_q, register_27_q, register_28_q, register_29_q, register_30_q, register_31_q,
       register_32_q;

  Decoder #(.enable("false"), .select(5)) decoder_1 (
    .out1(decoder_1_out1), .out2(decoder_1_out2), .out3(decoder_1_out3), .out4(decoder_1_out4),
    .out5(decoder_1_out5), .out6(decoder_1_out6), .out7(decoder_1_out7), .out8(decoder_1_out8),
    .out9(decoder_1_out9), .out10(decoder_1_out10), .out11(decoder_1_out11), .out12(decoder_1_out12),
    .out13(decoder_1_out13), .out14(decoder_1_out14), .out15(decoder_1_out15), .out16(decoder_1_out16),
    .out17(decoder_1_out17), .out18(decoder_1_out18), .out19(decoder_1_out19), .out20(decoder_1_out20),
    .out21(decoder_1_out21), .out22(decoder_1_out22), .out23(decoder_1_out23), .out24(decoder_1_out24),
    .out25(decoder_1_out25), .out26(decoder_1_out26), .out27(decoder_1_out27), .out28(decoder_1_out28),
    .out29(decoder_1_out29), .out30(decoder_1_out30), .out31(decoder_1_out31), .sel(writeReg));  // open: out0
  and and_1 (and_1_out, decoder_1_out1, RegWrite);
  and and_2 (and_2_out, decoder_1_out2, RegWrite);
  and and_3 (and_3_out, decoder_1_out3, RegWrite);
  and and_4 (and_4_out, decoder_1_out4, RegWrite);
  and and_5 (and_5_out, decoder_1_out5, RegWrite);
  and and_6 (and_6_out, decoder_1_out6, RegWrite);
  and and_7 (and_7_out, decoder_1_out7, RegWrite);
  Register #(.width(32)) register_1 (.Q(register_1_q), .clr(undriven));  // open: D, en, clk
  Register #(.width(32)) register_2 (.D(writeData), .en(and_1_out), .clk(clk), .Q(register_2_q), .clr(undriven_2));
  Register #(.width(32)) register_3 (.D(writeData), .en(and_2_out), .clk(clk), .Q(register_3_q), .clr(undriven_3));
  Register #(.width(32)) register_4 (.D(writeData), .en(and_3_out), .clk(clk), .Q(register_4_q));  // open: clr
  Register #(.width(32)) register_5 (.D(writeData), .en(and_4_out), .clk(clk), .Q(register_5_q));  // open: clr
  Register #(.width(32)) register_6 (.D(writeData), .en(and_5_out), .clk(clk), .Q(register_6_q));  // open: clr
  Register #(.width(32)) register_7 (.D(writeData), .en(and_6_out), .clk(clk), .Q(register_7_q));  // open: clr
  Register #(.width(32)) register_8 (.D(writeData), .en(and_7_out), .clk(clk), .Q(register_8_q));  // open: clr
  and and_8 (and_8_out, decoder_1_out8, RegWrite);
  and and_9 (and_9_out, decoder_1_out9, RegWrite);
  and and_10 (and_10_out, decoder_1_out10, RegWrite);
  and and_11 (and_11_out, decoder_1_out11, RegWrite);
  and and_12 (and_12_out, decoder_1_out12, RegWrite);
  and and_13 (and_13_out, decoder_1_out13, RegWrite);
  and and_14 (and_14_out, decoder_1_out14, RegWrite);
  and and_15 (and_15_out, decoder_1_out15, RegWrite);
  Register #(.width(32)) register_9 (.D(writeData), .en(and_8_out), .clk(clk), .Q(register_9_q));  // open: clr
  Register #(.width(32)) register_10 (.D(writeData), .en(and_9_out), .clk(clk), .Q(register_10_q));  // open: clr
  Register #(.width(32)) register_11 (.D(writeData), .en(and_10_out), .clk(clk), .Q(register_11_q));  // open: clr
  Register #(.width(32)) register_12 (.D(writeData), .en(and_11_out), .clk(clk), .Q(register_12_q));  // open: clr
  Register #(.width(32)) register_13 (.D(writeData), .en(and_12_out), .clk(clk), .Q(register_13_q));  // open: clr
  Register #(.width(32)) register_14 (.D(writeData), .en(and_13_out), .clk(clk), .Q(register_14_q));  // open: clr
  Register #(.width(32)) register_15 (.D(writeData), .en(and_14_out), .clk(clk), .Q(register_15_q));  // open: clr
  Register #(.width(32)) register_16 (.D(writeData), .en(and_15_out), .clk(clk), .Q(register_16_q));  // open: clr
  and and_16 (and_16_out, decoder_1_out16, RegWrite);
  and and_17 (and_17_out, decoder_1_out17, RegWrite);
  and and_18 (and_18_out, decoder_1_out18, RegWrite);
  and and_19 (and_19_out, decoder_1_out19, RegWrite);
  and and_20 (and_20_out, decoder_1_out20, RegWrite);
  and and_21 (and_21_out, decoder_1_out21, RegWrite);
  and and_22 (and_22_out, decoder_1_out22, RegWrite);
  and and_23 (and_23_out, decoder_1_out23, RegWrite);
  Register #(.width(32)) register_17 (.D(writeData), .en(and_16_out), .clk(clk), .Q(register_17_q));  // open: clr
  Register #(.width(32)) register_18 (.D(writeData), .en(and_17_out), .clk(clk), .Q(register_18_q));  // open: clr
  Register #(.width(32)) register_19 (.D(writeData), .en(and_18_out), .clk(clk), .Q(register_19_q));  // open: clr
  Register #(.width(32)) register_20 (.D(writeData), .en(and_19_out), .clk(clk), .Q(register_20_q));  // open: clr
  Register #(.width(32)) register_21 (.D(writeData), .en(and_20_out), .clk(clk), .Q(register_21_q));  // open: clr
  Register #(.width(32)) register_22 (.D(writeData), .en(and_21_out), .clk(clk), .Q(register_22_q));  // open: clr
  Register #(.width(32)) register_23 (.D(writeData), .en(and_22_out), .clk(clk), .Q(register_23_q));  // open: clr
  Register #(.width(32)) register_24 (.D(writeData), .en(and_23_out), .clk(clk), .Q(register_24_q));  // open: clr
  and and_24 (and_24_out, decoder_1_out24, RegWrite);
  and and_25 (and_25_out, decoder_1_out25, RegWrite);
  and and_26 (and_26_out, decoder_1_out26, RegWrite);
  and and_27 (and_27_out, decoder_1_out27, RegWrite);
  and and_28 (and_28_out, decoder_1_out28, RegWrite);
  and and_29 (and_29_out, decoder_1_out29, RegWrite);
  and and_30 (and_30_out, decoder_1_out30, RegWrite);
  and and_31 (and_31_out, decoder_1_out31, RegWrite);
  Register #(.width(32)) register_25 (.D(writeData), .en(and_24_out), .clk(clk), .Q(register_25_q));  // open: clr
  Register #(.width(32)) register_26 (.D(writeData), .en(and_25_out), .clk(clk), .Q(register_26_q));  // open: clr
  Register #(.width(32)) register_27 (.D(writeData), .en(and_26_out), .clk(clk), .Q(register_27_q));  // open: clr
  Register #(.width(32)) register_28 (.D(writeData), .en(and_27_out), .clk(clk), .Q(register_28_q));  // open: clr
  Register #(.width(32)) register_29 (.D(writeData), .en(and_28_out), .clk(clk), .Q(register_29_q));  // open: clr
  Register #(.width(32)) register_30 (.D(writeData), .en(and_29_out), .clk(clk), .Q(register_30_q));  // open: clr
  Register #(.width(32)) register_31 (.D(writeData), .en(and_30_out), .clk(clk), .Q(register_31_q));  // open: clr
  Register #(.width(32)) register_32 (.D(writeData), .en(and_31_out), .clk(clk), .Q(register_32_q));  // open: clr
  Multiplexer #(.select(5), .width(32)) multiplexer_1 (
    .in0(register_1_q), .in1(register_2_q), .in2(register_3_q), .in3(register_4_q), .in4(register_5_q),
    .in5(register_6_q), .in6(register_7_q), .in7(register_8_q), .in8(register_9_q), .in9(register_10_q),
    .in10(register_11_q), .in11(register_12_q), .in12(register_13_q), .in13(register_14_q),
    .in14(register_15_q), .in15(register_16_q), .in16(register_17_q), .in17(register_18_q),
    .in18(register_19_q), .in19(register_20_q), .in20(register_21_q), .in21(register_22_q),
    .in22(register_23_q), .in23(register_24_q), .in24(register_25_q), .in25(register_26_q),
    .in26(register_27_q), .in27(register_28_q), .in28(register_29_q), .in29(register_30_q),
    .in30(register_31_q), .in31(register_32_q), .out(read1), .sel(readReg1));
  Multiplexer #(.select(5), .width(32)) multiplexer_2 (
    .in0(register_1_q), .in1(register_2_q), .in2(register_3_q), .in3(register_4_q), .in4(register_5_q),
    .in5(register_6_q), .in6(register_7_q), .in7(register_8_q), .in8(register_9_q), .in9(register_10_q),
    .in10(register_11_q), .in11(register_12_q), .in12(register_13_q), .in13(register_14_q),
    .in14(register_15_q), .in15(register_16_q), .in16(register_17_q), .in17(register_18_q),
    .in18(register_19_q), .in19(register_20_q), .in20(register_21_q), .in21(register_22_q),
    .in22(register_23_q), .in23(register_24_q), .in24(register_25_q), .in25(register_26_q),
    .in26(register_27_q), .in27(register_28_q), .in28(register_29_q), .in29(register_30_q),
    .in30(register_31_q), .in31(register_32_q), .out(read2), .sel(readReg2));
endmodule

module ALU_32 (
  input  [2:0] Op,
  input  [31:0] A,
  input  [31:0] B,
  input  Sub,
  output [31:0] outputt
);

  wire [31:0] adder_1_out, adder_2_out, and_1_out, multiplexer_1_out, not_1_out, or_1_out, xor_1_out;

  assign not_1_out = ~B;  // NOT_Gate not_1, 32 bits wide
  Adder #(.width(32)) adder_1 (.a(not_1_out), .b(32'h1), .out(adder_1_out));  // open: cin, cout
  Multiplexer #(.width(32)) multiplexer_1 (.in0(B), .in1(adder_1_out), .out(multiplexer_1_out), .sel(Sub));
  assign and_1_out = A & B;  // AND_Gate and_1, 32 bits wide
  assign or_1_out = A | B;  // OR_Gate or_1, 32 bits wide
  assign xor_1_out = A ^ B;  // XOR_Gate xor_1, 32 bits wide
  Adder #(.width(32)) adder_2 (.a(A), .b(multiplexer_1_out), .out(adder_2_out));  // open: cin, cout
  Multiplexer #(.select(3), .width(32)) multiplexer_2 (
    .in1(and_1_out), .in2(or_1_out), .in3(xor_1_out), .in4(adder_2_out), .out(outputt), .sel(Op));  // open: in0, in5, in6, in7
endmodule

module Memory (
  input  writeSignal,
  input  readSignal,
  input  [31:0] address,
  input  clk,
  input  [31:0] data,
  output [31:0] read
);

  wire [15:0] bit_extender_1_out;

  Bit_Extender #(.in_width(32)) bit_extender_1 (.in(address), .out(bit_extender_1_out));
  RAM #(.addrWidth(16), .clearpin("true"), .dataWidth(32)) ram_1 (
    .addr(bit_extender_1_out), .we(writeSignal), .oe(readSignal), .clk(clk), .din(data), .dout(read));  // open: clr
endmodule

module ALUcontrol (
  input  [5:0] funct,
  input  [2:0] ALUop,
  output isSub,
  output [2:0] ALUcode
);

  wire add_out, AND1_out, and_1_out, and_3_out, and_4_out, and_5_out, decoder_1_out0, decoder_1_out1,
       decoder_1_out2, decoder_1_out3, decoder_1_out4, OR1_out, or_1_out, or_2_out, priority_encoder_1_p2,
       priority_encoder_1_p3, sub_out, XOR1_out;

  Decoder #(.enable("false"), .select(3)) decoder_1 (
    .out0(decoder_1_out0), .out1(decoder_1_out1), .out2(decoder_1_out2), .out3(decoder_1_out3),
    .out4(decoder_1_out4), .sel(ALUop));  // open: out5, out6, out7
  and add (add_out, funct[5], ~funct[4], ~funct[3], ~funct[2], ~funct[1], ~funct[0]);  // AND_Gate
  and and_1 (and_1_out, decoder_1_out0, add_out);
  or or_1 (or_1_out, decoder_1_out4, and_1_out, isSub);
  and and_2 (isSub, decoder_1_out0, sub_out);
  and sub (sub_out, funct[5], ~funct[4], ~funct[3], ~funct[2], funct[1], ~funct[0]);  // AND_Gate
  and AND1 (AND1_out, funct[5], ~funct[4], ~funct[3], funct[2], ~funct[1], ~funct[0]);  // AND_Gate
  and and_3 (and_3_out, decoder_1_out0, AND1_out);
  or or_2 (or_2_out, decoder_1_out1, and_3_out);
  // Priority_Encoder priority_encoder_1: pin names not known; wires that end beside it: or_2_out, priority_encoder_1_p2, priority_encoder_1_p3, ALUcode, or_1_out
  and OR1 (OR1_out, funct[5], ~funct[4], ~funct[3], funct[2], ~funct[1], funct[0]);  // AND_Gate
  and and_4 (and_4_out, decoder_1_out0, OR1_out);
  or or_3 (priority_encoder_1_p2, decoder_1_out2, and_4_out);
  and XOR1 (XOR1_out, funct[5], ~funct[4], ~funct[3], funct[2], funct[1], ~funct[0]);  // AND_Gate
  and and_5 (and_5_out, decoder_1_out0, XOR1_out);
  or or_4 (priority_encoder_1_p3, decoder_1_out3, and_5_out);
endmodule

module Control (
  input  [5:0] OPcode,
  output RegDst,
  output MemWrite,
  output MemRead,
  output Mem2Reg,
  output RegWrite,
  output ALUsrc,
  output [2:0] ALUop
);

  wire addi_out, andi_out, or_1_out, ori_out, xori_out;

  and R_type (RegDst, ~OPcode[5], ~OPcode[4], ~OPcode[3], ~OPcode[2], ~OPcode[1], ~OPcode[0]);  // AND_Gate
  and lw (Mem2Reg, OPcode[5], ~OPcode[4], ~OPcode[3], ~OPcode[2], OPcode[1], OPcode[0]);  // AND_Gate
  and sw (MemWrite, OPcode[5], ~OPcode[4], OPcode[3], ~OPcode[2], OPcode[1], OPcode[0]);  // AND_Gate
  or or_1 (or_1_out, Mem2Reg, MemWrite, addi_out);
  and addi (addi_out, ~OPcode[5], ~OPcode[4], OPcode[3], ~OPcode[2], ~OPcode[1], ~OPcode[0]);  // AND_Gate
  and andi (andi_out, ~OPcode[5], ~OPcode[4], OPcode[3], OPcode[2], ~OPcode[1], ~OPcode[0]);  // AND_Gate
  and ori (ori_out, ~OPcode[5], ~OPcode[4], OPcode[3], OPcode[2], ~OPcode[1], OPcode[0]);  // AND_Gate
  and xori (xori_out, ~OPcode[5], ~OPcode[4], OPcode[3], OPcode[2], OPcode[1], ~OPcode[0]);  // AND_Gate
  or or_2 (RegWrite, xori_out, ori_out, andi_out, addi_out, Mem2Reg, RegDst);
  or or_3 (ALUsrc, xori_out, ori_out, andi_out, addi_out, MemWrite, Mem2Reg);
  Priority_Encoder priority_encoder_1 (
    .in0(RegDst), .in1(andi_out), .in2(ori_out), .in3(xori_out), .in4(or_1_out), .out(ALUop));  // open: in5, in6, in7, en_in, gs, en_out

  assign MemRead = Mem2Reg;
endmodule

module Cache (
  input  [31:0] address,
  input  [31:0] update,
  input  clk,
  output [31:0] read,
  output hit
);

  wire and_1_out, and_2_out, and_3_out, and_4_out, and_5_out, and_6_out, and_7_out, and_8_out,
       bit_extender_2_out, bit_extender_3_out, bit_extender_4_out, bit_extender_5_out, decoder_1_out0,
       decoder_1_out1, decoder_1_out2, decoder_1_out3, decoder_2_out0, decoder_2_out1, decoder_2_out2,
       decoder_2_out3, missed_out;
  wire [1:0] adder_1_out, priority_encoder_1_out, register_1_q;
  wire [15:0] bit_extender_1_out, register_2_q, register_3_q, register_4_q, register_5_q, xnor_1_out,
       xnor_2_out, xnor_3_out, xnor_4_out;
  wire [31:0] register_6_q, register_7_q, register_8_q, register_9_q;

  Register #(.width(2)) register_1 (.D(adder_1_out), .en(missed_out), .clk(clk), .Q(register_1_q));  // open: clr
  Decoder #(.enable("false"), .select(2)) decoder_1 (
    .out0(decoder_1_out0), .out1(decoder_1_out1), .out2(decoder_1_out2), .out3(decoder_1_out3),
    .sel(register_1_q));
  Adder #(.width(2)) adder_1 (.a(2'b01), .b(register_1_q), .out(adder_1_out));  // open: cin, cout
  Bit_Extender #(.in_width(32)) bit_extender_1 (.in(address), .out(bit_extender_1_out));
  and and_1 (and_1_out, decoder_1_out0, missed_out);
  and and_2 (and_2_out, decoder_1_out1, missed_out);
  and and_3 (and_3_out, decoder_1_out2, missed_out);
  and and_4 (and_4_out, decoder_1_out3, missed_out);
  Register #(.width(16)) register_2 (.D(bit_extender_1_out), .en(and_1_out), .clk(clk), .Q(register_2_q));  // open: clr
  Register #(.width(16)) register_3 (.D(bit_extender_1_out), .en(and_2_out), .clk(clk), .Q(register_3_q));  // open: clr
  Register #(.width(16)) register_4 (.D(bit_extender_1_out), .en(and_3_out), .clk(clk), .Q(register_4_q));  // open: clr
  Register #(.width(16)) register_5 (.D(bit_extender_1_out), .en(and_4_out), .clk(clk), .Q(register_5_q));  // open: clr
  Bit_Extender #(.in_width(16), .out_width(1)) bit_extender_2 (.in(xnor_1_out), .out(bit_extender_2_out));
  assign xnor_1_out = ~(bit_extender_1_out ^ register_2_q);  // XNOR_Gate xnor_1, 16 bits wide
  Bit_Extender #(.in_width(16), .out_width(1)) bit_extender_3 (.in(xnor_2_out), .out(bit_extender_3_out));
  assign xnor_2_out = ~(bit_extender_1_out ^ register_3_q);  // XNOR_Gate xnor_2, 16 bits wide
  Bit_Extender #(.in_width(16), .out_width(1)) bit_extender_4 (.in(xnor_3_out), .out(bit_extender_4_out));
  assign xnor_3_out = ~(bit_extender_1_out ^ register_4_q);  // XNOR_Gate xnor_3, 16 bits wide
  Bit_Extender #(.in_width(16), .out_width(1)) bit_extender_5 (.in(xnor_4_out), .out(bit_extender_5_out));
  assign xnor_4_out = ~(bit_extender_1_out ^ register_5_q);  // XNOR_Gate xnor_4, 16 bits wide
  Decoder #(.enable("false"), .select(2)) decoder_2 (
    .out0(decoder_2_out0), .out1(decoder_2_out1), .out2(decoder_2_out2), .out3(decoder_2_out3),
    .sel(register_1_q));
  nor missed (missed_out, bit_extender_2_out, bit_extender_3_out, bit_extender_4_out, bit_extender_5_out);
  Priority_Encoder #(.select(2)) priority_encoder_1 (
    .in0(bit_extender_2_out), .in1(bit_extender_3_out), .in2(bit_extender_4_out), .in3(bit_extender_5_out),
    .out(priority_encoder_1_out));  // open: gs, en_out, en_in
  and and_5 (and_5_out, decoder_2_out3, missed_out);
  and and_6 (and_6_out, decoder_2_out2, missed_out);
  and and_7 (and_7_out, decoder_2_out1, missed_out);
  and and_8 (and_8_out, decoder_2_out0, missed_out);
  Register #(.width(32)) register_6 (.D(update), .en(and_5_out), .clk(clk), .Q(register_6_q));  // open: clr
  Register #(.width(32)) register_7 (.D(update), .en(and_6_out), .clk(clk), .Q(register_7_q));  // open: clr
  Register #(.width(32)) register_8 (.D(update), .en(and_7_out), .clk(clk), .Q(register_8_q));  // open: clr
  Register #(.width(32)) register_9 (.D(update), .en(and_8_out), .clk(clk), .Q(register_9_q));  // open: clr
  not not_1 (hit, missed_out);
  Multiplexer #(.select(2), .width(32)) multiplexer_1 (
    .in0(register_6_q), .in1(register_7_q), .in2(register_8_q), .in3(register_9_q), .out(read),
    .sel(priority_encoder_1_out));

  // Notes on the sheet:
  //   addresses
  //   datas
endmodule
